// Logisim project Part D.circ as structural Verilog: 1 circuit, main circuit main
module main (
  input  A,
  input  B,
  input  C,
  output out_4
);

  wire and_1_out, and_2_out, nor_1_out, not_1_out, not_2_out, or_1_out;

  and and_1 (and_1_out, A, B);
  and and_2 (and_2_out, B, C);
  not not_1 (not_1_out, A);
  not not_2 (not_2_out, C);
  or or_1 (or_1_out, not_1_out, and_2_out);
  nor nor_1 (nor_1_out, and_1_out, not_2_out);
  nand nand_1 (out_4, or_1_out, nor_1_out);

  // Notes on the sheet:
  //   ((A'+BC)(AB+C')')'
endmodule
